# Fritzing sketch 5vRegulator317 (saved by Fritzing 0.9.2b)
circuit board: 5.17162cm x 2.02256cm
breadboards: 1

parts:
  C2 = Electrolytic Capacitor [capacitance=10µF package="100 mil [THT, electrolytic]"]
  C3 = Electrolytic Capacitor [capacitance=1µF package="100 mil [THT, electrolytic]"]
  317 = Voltage Regulator - Variable [package="TO220 [THT]"]
  R1 = Resistor [tolerance=±5% resistance=330 package=THT]
  R2 = Resistor [tolerance=±5% resistance=1k package=THT]
  D1 = Rectifier Diode [part_number=1N4001 package="300 mil [THT]"]
  D2 = Rectifier Diode [part_number=1N4001 package="300 mil [THT]"]
  VIN = mystery part, 3 pins [chip_label=?]
  GND = mystery part, 3 pins [chip_label=?]
  J1 = Screw terminal - 2 pins [package=THT]
  C1 = Ceramic Capacitor [capacitance=100nF package="200 mil [THT, multilayer]"]

nets:
  N1: C2.-, C3.-, R2.Pin_0, GND.pin1, GND.pin2, GND.pin3, J1.pin1, C1.0
  N2: C2.+, 317.ADJ, R1.Pin_0, R2.Pin_1, D2.anode
  N3: C3.+, 317.OUT, R1.Pin_1, D1.anode, D2.cathode, J1.pin2
  N4: 317.IN, D1.cathode, VIN.pin1, VIN.pin2, VIN.pin3, C1.1

notes:
  1
  3
  6
  9
  12
  15
  18
  A
  B
  C
  D
  E
  F
