# Fritzing sketch MotorController (saved by Fritzing 0.9.2b)
circuit board: 5cm x 7cm
breadboards: 1

parts:
  HK19F = mystery part, 16 pins [chip_label="DPDT Relay"]
  MotorOut1 = mystery part, 3 pins [chip_label="Spade Connector"]
  Q2 = TRANSISTOR_NPN [package=to-92-ammo]
  +18v_VCC = mystery part, 3 pins [chip_label="Spade Connector"]
  D1 = Diode [package=diode-1n4148]
  R1 = Resistor [tolerance=±5% resistance=10k package=THT]
  Q1 = Basic FET N-Channel [package="TO220 [THT]"]
  Q3 = Basic FET N-Channel [package="TO220 [THT]"]
  R3 = Resistor [tolerance=±5% resistance=1k package=THT]
  HK19F1 = mystery part, 16 pins [chip_label="DPDT Relay"]
  MotorOut4 = mystery part, 3 pins [chip_label="Spade Connector"]
  MotorOut3 = mystery part, 3 pins [chip_label="Spade Connector"]
  Q4 = TRANSISTOR_NPN [package=to-92-ammo]
  D2 = Diode [package=diode-1n4148]
  R2 = Resistor [tolerance=±5% resistance=10k package=THT]
  ATTiny85 = attiny85 [package=dip]
  R5 = Resistor [tolerance=±5% resistance=10k package=THT]
  7805 = Voltage Regulator - 5V [package="TO220 [THT]"]
  R4 = Resistor [tolerance=±5% resistance=10k package=THT]
  RX = male pin header, 1 pin [form="♂ (male)"]
  C1 = Electrolytic Capacitor [capacitance=10µF package="100 mil [THT, electrolytic]"]
  C2 = Ceramic Capacitor [capacitance=1µF package="100 mil [THT, multilayer]"]
  MotorOut2 = mystery part, 3 pins [chip_label="Spade Connector"]
  C3 = Electrolytic Capacitor [capacitance=47µF package="100 mil [THT, electrolytic]"]
  D3 = Rectifier Diode [part_number=1N4001 package="300 mil [THT]"]
  D4 = Rectifier Diode [part_number=1N4001 package="300 mil [THT]"]
  C4 = Electrolytic Capacitor [capacitance=47µF package="100 mil [THT, electrolytic]"]
  GROUND = mystery part, 3 pins [chip_label="Spade Connector"]

nets:
  N1: HK19F.pin1, Q2.C, D1.A
  N2: HK19F.pin4, Q1.drain
  N3: HK19F.pin6, HK19F.pin9, MotorOut1.pin1, MotorOut1.pin2, MotorOut1.pin3
  N4: HK19F.pin8, HK19F.pin11, MotorOut2.pin1, MotorOut2.pin2, MotorOut2.pin3
  N5: HK19F.pin13, D3.cathode
  N6: HK19F.pin16, D1.C, HK19F1.pin16, D2.C, ATTiny85.Pin_8, R5.Pin_0, 7805.output_voltage, C2.1
  N7: Q2.E, Q1.source, Q3.source, Q4.E, R2.Pin_1, ATTiny85.Pin_4, 7805.GND, R4.Pin_0, C1.-, C2.0, C3.-, C4.-, GROUND.pin1, GROUND.pin2, GROUND.pin3
  N8: Q2.B, R1.Pin_0
  N9: +18v_VCC.pin1, +18v_VCC.pin2, +18v_VCC.pin3, 7805.input_voltage, C1.+, C3.+, D3.anode, D4.anode, C4.+
  N10: R1.Pin_1, ATTiny85.Pin_3
  N11: Q1.gate, R2.Pin_0, ATTiny85.Pin_6
  N12: Q3.gate, ATTiny85.Pin_5, R4.Pin_1
  N13: Q3.drain, HK19F1.pin4
  N14: R3.Pin_0, ATTiny85.Pin_2
  N15: R3.Pin_1, Q4.B
  N16: HK19F1.pin1, Q4.C, D2.A
  N17: HK19F1.pin6, HK19F1.pin9, MotorOut3.pin1, MotorOut3.pin2, MotorOut3.pin3
  N18: HK19F1.pin8, HK19F1.pin11, MotorOut4.pin1, MotorOut4.pin2, MotorOut4.pin3
  N19: HK19F1.pin13, D4.cathode
  N20: ATTiny85.Pin_1, R5.Pin_1
  N21: ATTiny85.Pin_7, RX.pin1

notes:
  DPDT Relay
  5V
  DIR
  PWM
  GND
  Dual Motor Controller
  Copyright ©2015 That Ain't Working
  All RIghts Reserved
