# Fritzing sketch MotorController2 (saved by Fritzing 0.9.2b)
circuit board: 6.62282cm x 5.30008cm
breadboards: 1

parts:
  MotorDir2 = mystery part, 3 pins [chip_label="Spade Connector"]
  VCC = mystery part, 3 pins [chip_label="Spade Connector"]
  R4 = Resistor [tolerance=±5% resistance=1k package=THT]
  Q2 = Basic FET N-Channel [package="TO220 [THT]"]
  Q1 = Basic FET N-Channel [package="TO220 [THT]"]
  R3 = Resistor [tolerance=±5% resistance=1k package=THT]
  MotorPWM1 = mystery part, 3 pins [chip_label="Spade Connector"]
  MotorDir1 = mystery part, 3 pins [chip_label="Spade Connector"]
  R1 = Resistor [tolerance=±5% resistance=1k package=THT]
  ATTiny85 = attiny85 [package=dip]
  R5 = Resistor [tolerance=±5% resistance=10k package=THT]
  7805 = Voltage Regulator - 5V [package="TO220 [THT]"]
  RX = male pin header, 1 pin [form="♂ (male)"]
  C1 = Electrolytic Capacitor [capacitance=10µF package="100 mil [THT, electrolytic]"]
  C2 = Ceramic Capacitor [capacitance=1µF package="100 mil [THT, multilayer]"]
  MotorPWM2 = mystery part, 3 pins [chip_label="Spade Connector"]
  GND = mystery part, 3 pins [chip_label="Spade Connector"]
  Q4 = Basic FET N-Channel [package="TO220 [THT]"]
  Q3 = Basic FET N-Channel [package="TO220 [THT]"]
  GND_2 = male pin header, 1 pin [form="♂ (male)"]
  R2 = Resistor [tolerance=±5% resistance=1k package=THT]
  D1 = BYV25X Diode [part_number=BYV25X package=THT]
  D2 = BYV25X Diode [part_number=BYV25X package=THT]
  D3 = BYV25X Diode [part_number=BYV25X package=THT]
  D4 = BYV25X Diode [part_number=BYV25X package=THT]
  F1 = Resettable Fuse PTC [package=ptc]
  F2 = Resettable Fuse PTC [package=ptc]
  R6 = Resistor [tolerance=±5% resistance=10k package=THT]
  R7 = Resistor [tolerance=±5% resistance=10k package=THT]
  R8 = Resistor [tolerance=±5% resistance=10k package=THT]
  R9 = Resistor [tolerance=±5% resistance=10k package=THT]
  R10 = Resistor [tolerance=±5% resistance=10k package=THT]
  D5 = Diode [package=diode-1n4148]

nets:
  N1: MotorDir2.pin1, MotorDir2.pin2, MotorDir2.pin3, D2.a
  N2: VCC.pin1, VCC.pin2, VCC.pin3, 7805.input_voltage, C1.+
  N3: R4.Pin_0, ATTiny85.Pin_3
  N4: R4.Pin_1, Q4.gate, R9.Pin_0
  N5: Q2.gate, R2.Pin_0, R7.Pin_1
  N6: Q2.drain, D4.k
  N7: Q2.source, Q1.source, ATTiny85.Pin_4, 7805.GND, C1.-, C2.0, GND.pin1, GND.pin2, GND.pin3, Q4.source, Q3.source, GND_2.pin1, R6.Pin_0, R7.Pin_0, R8.Pin_1, R9.Pin_1, R10.Pin_1
  N8: Q1.gate, R1.Pin_1, R6.Pin_1
  N9: Q1.drain, D3.k
  N10: R3.Pin_0, ATTiny85.Pin_2
  N11: R3.Pin_1, Q3.gate, R8.Pin_0
  N12: MotorPWM1.pin1, MotorPWM1.pin2, MotorPWM1.pin3, F1.1
  N13: MotorDir1.pin1, MotorDir1.pin2, MotorDir1.pin3, D1.a
  N14: R1.Pin_0, ATTiny85.Pin_6
  N15: ATTiny85.Pin_1, R5.Pin_1
  N16: ATTiny85.Pin_5, R2.Pin_1
  N17: ATTiny85.Pin_7, R10.Pin_0, D5.C
  N18: ATTiny85.Pin_8, R5.Pin_0, 7805.output_voltage, C2.1
  N19: RX.pin1, D5.A
  N20: MotorPWM2.pin1, MotorPWM2.pin2, MotorPWM2.pin3, F2.1
  N21: Q4.drain, D2.k
  N22: Q3.drain, D1.k
  N23: D3.a, F1.2
  N24: D4.a, F2.2

notes:
  DPDT Relay
  5V
  DIR
  PWM
  GND
  Dual Motor Controller
  All Rights Reserved
  Version 2.2
  Dual Motor Controller v2.2
  ©2015 That Ain't Working
  with Off-Board Relays
  ©2015 That Ain't Working, All Rights Reserved
  From Relay Coils
  From Relay Throws
  Power Input
  From Serial TX

custom parts:
  BYV25X Diode: BYV25X ultrafast rectifier diode 600V, 5-10A
