# Fritzing sketch MotorController3 (saved by Fritzing 0.9.2b)
circuit board: 9cm x 7cm
breadboards: 1

parts:
  Q2 = Basic FET N-Channel [package="TO220 [THT]"]
  R1 = Resistor [tolerance=±5% resistance=10k package=THT]
  C2 = Electrolytic Capacitor [capacitance=47µF voltage=20V package="100 mil [THT, electrolytic]"]
  C1 = Electrolytic Capacitor [capacitance=47µF voltage=50V package="100 mil [THT, electrolytic]"]
  I2C = Screw terminal - 2 pins [package=THT]
  Relay_Out = screw terminal, 2 pins [part_number="Screw Connector"]  # not connected
  Relay_Coil = screw terminal, 2 pins [part_number="Screw Connector"]
  Relay_Pole_2 = screw terminal, 2 pins [part_number="Screw Connector"]
  Relay_Pole_1 = screw terminal, 2 pins [part_number="Screw Connector"]
  Q1 = Basic FET N-Channel [package="TO220 [THT]"]
  R2 = Resistor [tolerance=±5% resistance=1k package=THT]
  R3 = Resistor [tolerance=±5% resistance=10k package=THT]
  D1 = BYV25X Diode [part_number=BYV25x package=THT]
  D2 = BYV25X Diode [part_number=BYV25X package=THT]
  J1 = mystery part, 3 pins [chip_label=? part_number=Jumper]
  ATtiny85 = attiny85 [package=dip]
  R4 = Resistor [tolerance=±5% resistance=1k package=THT]
  R5 = Resistor [tolerance=±5% resistance=10k package=THT]
  C3 = Ceramic Capacitor [capacitance=100nF voltage=10V package="100 mil [THT, multilayer]"]
  V1 = Voltage Regulator - 3.3V [part_number=LM7833 package="TO220 [THT]"]
  VIN = mystery part, 3 pins [chip_label=? part_number="Spade Connector"]
  GND = mystery part, 3 pins [chip_label=? part_number="Spade Connector"]

nets:
  N1: Q2.gate, R4.Pin_1, R5.Pin_1
  N2: Q2.drain, D2.k
  GND: Q2.source, C2.-, C1.-, Q1.source, R3.Pin_1, J1.pin3, ATtiny85.Pin_4, R5.Pin_0, C3.0, V1.GND, GND.pin1, GND.pin2, GND.pin3
  N3: R1.Pin_0, J1.pin1, ATtiny85.Pin_1
  N4: R1.Pin_1, C2.+, ATtiny85.Pin_8, C3.1, V1.output_voltage
  18V: C1.+, Relay_Coil.pin1, Relay_Pole_2.pin1, Relay_Pole_1.pin2, V1.input_voltage, VIN.pin1, VIN.pin2, VIN.pin3
  N5: I2C.pin1, ATtiny85.Pin_7
  N6: I2C.pin2, ATtiny85.Pin_5
  N7: Relay_Coil.pin2, D1.a
  N8: Relay_Pole_2.pin2, Relay_Pole_1.pin1, D2.a
  N9: Q1.gate, R2.Pin_0, R3.Pin_0
  N10: Q1.drain, D1.k
  N11: R2.Pin_1, ATtiny85.Pin_6
  N12: J1.pin2, ATtiny85.Pin_2
  N13: ATtiny85.Pin_3, R4.Pin_0

notes:
  to motor
  SCL
  SDA
  Motor Controller 3.0
  ©2015 That Ain't Working
  All Rights Reserved
  R . L

custom parts:
  BYV25X Diode: BYV25X ultrafast rectifier diode 600V, 5-10A
