# Fritzing sketch MotorController4 (saved by Fritzing 0.9.2b)
circuit board: 9.46575cm x 5.25349cm
stripboards: 1

parts:
  Q2 = Basic FET N-Channel [package="TO220 [THT]"]
  Q4 = Basic FET N-Channel [package="TO220 [THT]"]
  Q3 = Basic FET N-Channel [package="TO220 [THT]"]
  Q1 = Basic FET N-Channel [package="TO220 [THT]"]
  VIN = mystery part, 3 pins [chip_label=? part_number=Spade]
  GND = mystery part, 3 pins [chip_label=? part_number=Spade]
  V5 = Voltage Regulator - 5V [part_number=LM7805 package="TO220 [THT]"]
  C3 = Ceramic Capacitor [capacitance=100nF package="100 mil [THT, multilayer]"]
  R1 = Resistor [tolerance=±5% resistance=1k package=THT]
  R2 = Resistor [tolerance=±5% resistance=10k package=THT]
  R3 = Resistor [tolerance=±5% resistance=1k package=THT]
  R4 = Resistor [tolerance=±5% resistance=10k package=THT]
  R7 = Resistor [tolerance=±5% resistance=1k package=THT]
  R5 = Resistor [tolerance=±5% resistance=1k package=THT]
  R6 = Resistor [tolerance=±5% resistance=10k package=THT]
  R8 = Resistor [tolerance=±5% resistance=10k package=THT]
  RDIR = mystery part, 3 pins [chip_label=? part_number=Spade]
  LDIR = mystery part, 3 pins [chip_label=? part_number=Spade]
  LPWM = mystery part, 3 pins [chip_label=? part_number=Spade]
  D2 = BYV25X Diode [part_number=BYV25X package=THT]
  R9 = Resistor [tolerance=±5% resistance=10k package=THT]
  Y1 = CRYSTAL [part_number=16MHz package=hc49u-v]
  C1 = Electrolytic Capacitor [capacitance=47µF package="100 mil [THT, electrolytic]"]
  ATmega328 = atmega328 [package=dip]
  C4 = Ceramic Capacitor [capacitance=10pF package="100 mil [THT, multilayer]"]
  C5 = Ceramic Capacitor [capacitance=10pF package="100 mil [THT, multilayer]"]
  D4 = BYV25X Diode [part_number=BYV25X package=THT]
  C2 = Electrolytic Capacitor [capacitance=47µF package="100 mil [THT, electrolytic]"]
  I2C = mystery part, 6 pins [chip_label=? part_number="Connector Block"]
  D3 = Rectifier Diode [part_number=1N4001 package="300 mil [THT]"]
  D1 = Rectifier Diode [part_number=1N4001 package="300 mil [THT]"]
  RPWM = mystery part, 3 pins [chip_label=? part_number=Spade]

nets:
  N1: Q2.gate, R3.Pin_1, R4.Pin_1
  N2: Q2.drain, D2.k
  GND: Q2.source, Q4.source, Q3.source, Q1.source, GND.pin1, GND.pin2, GND.pin3, V5.GND, C3.0, R2.Pin_1, R4.Pin_0, R6.Pin_0, R8.Pin_1, C1.-, ATmega328.GND, C4.1, C5.1, C2.-, I2C.pin4
  N3: Q4.gate, R7.Pin_1, R8.Pin_0
  N4: Q4.drain, D4.k
  N5: Q3.gate, R5.Pin_0, R6.Pin_1
  N6: Q3.drain, D3.cathode
  N7: Q1.gate, R1.Pin_0, R2.Pin_0
  N8: Q1.drain, D1.cathode
  N9: VIN.pin1, VIN.pin2, VIN.pin3, V5.input_voltage, C1.+
  N10: V5.output_voltage, C3.1, R9.Pin_1, ATmega328.VCC, ATmega328.AVCC, ATmega328.AREF, C2.+, I2C.pin3
  N11: R1.Pin_1, ATmega328.D10_(PWM)
  N12: R3.Pin_0, ATmega328.D11_(PWM)
  N13: R7.Pin_0, ATmega328.D6_(PWM)
  N14: R5.Pin_1, ATmega328.D7
  N15: RDIR.pin1, RDIR.pin2, RDIR.pin3, D1.anode
  N16: LDIR.pin1, LDIR.pin2, LDIR.pin3, D3.anode
  N17: LPWM.pin1, LPWM.pin2, LPWM.pin3, D4.a
  N18: D2.a, RPWM.pin1, RPWM.pin2, RPWM.pin3
  N19: R9.Pin_0, ATmega328.RESET
  N20: Y1.1, ATmega328.XLAT1, C4.0
  N21: Y1.2, ATmega328.XLAT2, C5.0
  N22: ATmega328.D0_(RX), I2C.pin5
  N23: ATmega328.D1_(TX), I2C.pin6
  N24: ATmega328.A4, I2C.pin2
  N25: ATmega328.A5, I2C.pin1

notes:
  SCL
  SDA
  VCC
  GND
  RXD
  TXD
  Dual Motor Controller
  Version 4.0
  ©2015 That Ain't Working
  All Rights Reserved
  Dual Motor Controller (I2C), ©2015 That Ain't Working, All Rights Reserved, 4.0

custom parts:
  BYV25X Diode: BYV25X ultrafast rectifier diode 600V, 5-10A
