# Fritzing sketch MotorController5 (saved by Fritzing 0.9.2b)
circuit board: 9.46575cm x 5.25349cm
stripboards: 1

parts:
  Q2 = Basic FET N-Channel [package="TO220 [THT]"]
  Q4 = Basic FET N-Channel [package="TO220 [THT]"]
  Q3 = Basic FET N-Channel [package="TO220 [THT]"]
  Q1 = Basic FET N-Channel [package="TO220 [THT]"]
  VIN = mystery part, 3 pins [chip_label=?]
  GND = mystery part, 3 pins [chip_label=?]
  V3 = Voltage Regulator - 5V [package="TO220 [THT]"]
  C3 = Ceramic Capacitor [capacitance=100nF package="100 mil [THT, multilayer]"]
  R1 = Resistor [tolerance=±5% resistance=1k package=THT]
  R2 = Resistor [tolerance=±5% resistance=10k package=THT]
  R3 = Resistor [tolerance=±5% resistance=1k package=THT]
  R4 = Resistor [tolerance=±5% resistance=10k package=THT]
  R7 = Resistor [tolerance=±5% resistance=1k package=THT]
  R5 = Resistor [tolerance=±5% resistance=1k package=THT]
  R6 = Resistor [tolerance=±5% resistance=10k package=THT]
  R8 = Resistor [tolerance=±5% resistance=10k package=THT]
  RPWM = mystery part, 3 pins [chip_label=?]
  RDIR = mystery part, 3 pins [chip_label=?]
  LDIR = mystery part, 3 pins [chip_label=?]
  LPWM = mystery part, 3 pins [chip_label=?]
  D2 = BYV25X Diode [package=THT]
  C1 = Electrolytic Capacitor [capacitance=47µF package="100 mil [THT, electrolytic]"]
  D4 = BYV25X Diode [package=THT]
  C2 = Electrolytic Capacitor [capacitance=47µF package="100 mil [THT, electrolytic]"]
  D3 = Rectifier Diode [part_number=1N4001 package="300 mil [THT]"]
  D1 = Rectifier Diode [part_number=1N4001 package="300 mil [THT]"]
  MSP430G2553 = MSP430G2 [part_number=MSP420G2 package=THT]
  I2C = mystery part, 6 pins [chip_label=?]

nets:
  N1: Q2.gate, R3.Pin_1, R4.Pin_1
  N2: Q2.drain, D2.k
  N3: Q2.source, Q4.source, Q3.source, Q1.source, GND.pin1, GND.pin2, GND.pin3, V3.GND, C3.1, R2.Pin_1, R4.Pin_0, R6.Pin_0, R8.Pin_1, C1.-, C2.-, MSP430G2553.pin20, I2C.pin3
  N4: Q4.gate, R7.Pin_1, R8.Pin_0
  N5: Q4.drain, D4.k
  N6: Q3.gate, R5.Pin_0, R6.Pin_1
  N7: Q3.drain, D3.cathode
  N8: Q1.gate, R1.Pin_0, R2.Pin_0
  N9: Q1.drain, D1.cathode
  N10: VIN.pin1, VIN.pin2, VIN.pin3, V3.input_voltage, C1.+
  N11: V3.output_voltage, C3.0, C2.+, MSP430G2553.pin1, MSP430G2553.pin16, I2C.pin4
  N12: R1.Pin_1, MSP430G2553.pin11
  N13: R3.Pin_0, MSP430G2553.pin12
  N14: R7.Pin_0, MSP430G2553.pin9
  N15: R5.Pin_1, MSP430G2553.pin10
  N16: RPWM.pin1, RPWM.pin2, RPWM.pin3, D2.a
  N17: RDIR.pin1, RDIR.pin2, RDIR.pin3, D1.anode
  N18: LDIR.pin1, LDIR.pin2, LDIR.pin3, D3.anode
  N19: LPWM.pin1, LPWM.pin2, LPWM.pin3, D4.a
  N20: MSP430G2553.pin3, I2C.pin1
  N21: MSP430G2553.pin4, I2C.pin2
  N22: MSP430G2553.pin14, I2C.pin6
  N23: MSP430G2553.pin15, I2C.pin5

notes:
  SCL
  SDA
  VCC
  GND
  Dual Motor Controller
  Version 5.0
  ©2015 That Ain't Working
  All Rights Reserved
  TXD
  RXD

custom parts:
  BYV25X Diode: BYV25X ultrafast rectifier diode 600V, 5-10A
  MSP430G2: MSP430G2 Microcontroller by Texas Instruments. Off LunchPad
