# Fritzing sketch MotorController6 (saved by Fritzing 0.9.2b)
circuit board: 4.5cm x 4.5cm
circuit board: 6cm x 4.5cm
breadboards: 1

parts:
  RESET = Pushbutton [package="[THT]"]
  R1 = Resistor [tolerance=±5% resistance=10k package=THT]
  R2 = Resistor [tolerance=±5% resistance=4.7k package=THT]
  R5 = Resistor [tolerance=±5% resistance=4.7k package=THT]
  R4 = Resistor [tolerance=±5% resistance=4.7k package=THT]
  R3 = Resistor [tolerance=±5% resistance=4.7k package=THT]
  Q1 = pnp-Powertransistor [part_number=TIP142 package="TO220 [THT]"]
  Q2 = NPN-Transistor [part_number=LM3904 package="TO92 [THT]"]
  R8 = Resistor [tolerance=±5% resistance=10k package=THT]
  D1 = BYV25X Diode [part_number=BYV25X package=THT]
  GND = male pin header, 3 pins [form="♂ (male)"]
  OUT = male pin header, 3 pins [form="♂ (male)"]
  IN = male pin header, 3 pins [form="♂ (male)"]
  COIL = male pin header, 3 pins [form="♂ (male)"]
  VIN = male pin header, 3 pins [form="♂ (male)"]
  Raspberry_Pi_GPIO = double row female pin header, 40 pins [form="♀ (female)"]
  MSP430G2 = MSP430G2 [part_number=MSP420G2 package=THT]
  J1 = female pin header, 2 pins [form="♀ (female)"]
  J1_2 = female pin header, 4 pins [form="♀ (female)"]

nets:
  N1: RESET.Pin_1, RESET.Pin_2, Raspberry_Pi_GPIO.pin28
  N2: RESET.Pin_3, RESET.Pin_4, R1.Pin_1, MSP430G2.pin16
  N3: R1.Pin_0, Raspberry_Pi_GPIO.pin40, MSP430G2.pin1
  N4: R2.Pin_0, J1_2.pin1
  N5: R2.Pin_1, MSP430G2.pin7
  N6: R5.Pin_0, J1_2.pin4
  N7: R5.Pin_1, MSP430G2.pin8
  N8: R4.Pin_0, J1_2.pin3
  N9: R4.Pin_1, MSP430G2.pin10
  N10: R3.Pin_0, J1_2.pin2
  N11: R3.Pin_1, MSP430G2.pin9
  N12: Q1.base, R8.Pin_0, J1.pin1
  N13: Q1.collector, D1.a, IN.pin1, IN.pin2, IN.pin3
  N14: Q1.emitter, Q2.E, R8.Pin_1, GND.pin1, GND.pin2, GND.pin3
  N15: Q2.B, J1.pin2
  N16: Q2.C, COIL.pin1, COIL.pin2, COIL.pin3
  N17: D1.k, OUT.pin1, OUT.pin2, OUT.pin3, VIN.pin1, VIN.pin2, VIN.pin3
  N18: Raspberry_Pi_GPIO.pin4, MSP430G2.pin3
  N19: Raspberry_Pi_GPIO.pin5, MSP430G2.pin4
  N20: Raspberry_Pi_GPIO.pin36, MSP430G2.pin20
  N21: Raspberry_Pi_GPIO.pin38, MSP430G2.pin14
  N22: Raspberry_Pi_GPIO.pin39, MSP430G2.pin15

notes:
  Motor
  PWM
  DIR
  LDIR
  LPWM
  RDIR
  RPWM
  *HEATSINK*
  Dual Motor Controller
  Version 6.0
  ©2015 That Ain't Working, All Rights Reserved
  Motor Driver
  ©2015 That Ain't Working
  All Rights Reserved
  Dalek, Dual Motor Controller/Motor Driver, 6.0

custom parts:
  BYV25X Diode: BYV25X ultrafast rectifier diode 600V, 5-10A
  MSP430G2: MSP430G2 Microcontroller by Texas Instruments. Off LunchPad
